# Fritzing sketch ArduinoLEDSketch (saved by Fritzing 0.9.2b)
breadboards: 1

parts:
  Part1 = Arduino Uno (Rev3) - ICSP
  LED1 = LEDs [package=led10mm]  # not connected
  J1 = Piezo Speaker

nets:
  N1: Part1.D8, J1.pin2
  N2: Part1.GND, J1.pin1
